// Logisim project prac-5_PDDJOH001.circ as structural Verilog: 1 circuit, main circuit main
module main (
  input  _1,
  input  _0,
  input  A1,
  input  A0,
  input  B1,
  input  B0,
  input  F2,
  input  F1,
  input  F0
);

  wire adder_1_cout, adder_1_out, adder_2_out, and_1_out, and_2_out, multiplexer_1_out, multiplexer_2_out,
       multiplexer_3_out, multiplexer_4_out, multiplexer_5_out, multiplexer_6_out, multiplexer_7_out,
       multiplexer_8_out, multiplexer_9_out, multiplexer_10_out, or_1_out, or_2_out, xor_1_out, xor_2_out;

  Multiplexer multiplexer_1 (.in0(B0), .in1(_1), .out(multiplexer_1_out), .sel(F1));  // open: en
  Multiplexer multiplexer_2 (.in0(B1), .in1(_0), .out(multiplexer_2_out), .sel(F1));  // open: en
  xor xor_1 (xor_1_out, multiplexer_1_out, F0);
  xor xor_2 (xor_2_out, multiplexer_2_out, F0);
  Adder #(.width(1)) adder_1 (.a(A0), .b(xor_1_out), .out(adder_1_out), .cin(F0), .cout(adder_1_cout));
  Adder #(.width(1)) adder_2 (.a(A1), .b(xor_2_out), .out(adder_2_out), .cin(adder_1_cout));  // open: cout
  Multiplexer multiplexer_3 (.in0(A0), .in1(_0), .out(multiplexer_3_out), .sel(F0));  // open: en
  Multiplexer multiplexer_4 (.in0(_0), .in1(A1), .out(multiplexer_4_out), .sel(F0));  // open: en
  and and_1 (and_1_out, A0, B0);
  and and_2 (and_2_out, A1, B1);
  or or_1 (or_1_out, A0, B0);
  or or_2 (or_2_out, A1, B1);
  Multiplexer multiplexer_5 (.in0(and_1_out), .in1(or_1_out), .out(multiplexer_5_out), .sel(F0));  // open: en
  Multiplexer multiplexer_6 (.in0(and_2_out), .in1(or_2_out), .out(multiplexer_6_out), .sel(F0));  // open: en
  Multiplexer multiplexer_7 (
    .in0(multiplexer_4_out), .in1(multiplexer_5_out), .out(multiplexer_7_out), .sel(F1));  // open: en
  Multiplexer multiplexer_8 (
    .in0(multiplexer_3_out), .in1(multiplexer_6_out), .out(multiplexer_8_out), .sel(F1));  // open: en
  Multiplexer multiplexer_9 (
    .in0(adder_1_out), .in1(multiplexer_7_out), .out(multiplexer_9_out), .sel(F2));  // open: en
  Multiplexer multiplexer_10 (
    .in0(adder_2_out), .in1(multiplexer_8_out), .out(multiplexer_10_out), .sel(F2));  // open: en
  // Probe on multiplexer_9_out
  // Probe on multiplexer_10_out

  // Notes on the sheet:
  //   A
  //   B
  //   FUNCTION SELECT
  //   2 bit adder/subtractor
  //   2 bit shifter
  //   2 bitwise and
  //   2 bitwise or
  //   Select between bitwise
  //   OR or AND
  //   And the rest of the logic
  //   Select between Shifter
  //   And the bitwise logic
  //   Select between Adder/subtractor
  //   OUTPUT
endmodule
